// Logisim project full_adder.circ as structural Verilog: 3 circuits, main circuit main
module main (
  input  [3:0] in_1,
  input  [3:0] in_2,
  input  En,
  output [3:0] out_4
);

  wire clock_1_out, Reset_out;
  wire [3:0] register_1_q, register_2_q, somador_8b_1_s;

  // Probe on in_1
  // Probe on in_2
  Clock clock_1 (.out(clock_1_out));
  Button Reset (.out(Reset_out));
  Register #(.width(4)) register_1 (.D(in_1), .en(En), .Q(register_1_q), .clk(clock_1_out), .clr(Reset_out));
  Register #(.width(4)) register_2 (.D(in_2), .en(En), .Q(register_2_q), .clk(clock_1_out), .clr(Reset_out));
  // Probe on register_1_q
  somador_8b somador_8b_1 (.B(register_1_q), .A(register_2_q), .Cin(1'b0), .S(somador_8b_1_s));  // open: Cout
  // Probe on register_2_q
  // Probe on out_4
  Register #(.width(4)) register_3 (.D(somador_8b_1_s), .en(En), .Q(out_4), .clk(clock_1_out), .clr(Reset_out));
endmodule

module somador_completo_1b (
  input  A,
  input  B,
  input  Cin,
  output S,
  output Cout
);

  wire and_1_out, and_2_out, and_3_out, or_1_out, xor_1_out;

  xor xor_1 (xor_1_out, A, B);
  and and_1 (and_1_out, A, B);
  and and_2 (and_2_out, A, Cin);
  and and_3 (and_3_out, B, Cin);
  xor xor_2 (S, xor_1_out, Cin);
  or or_1 (or_1_out, and_1_out, and_2_out);
  or or_2 (Cout, or_1_out, and_3_out);
endmodule

module somador_8b (
  input  Cin,
  input  [3:0] A,
  input  [3:0] B,
  output [3:0] S,
  output Cout
);

  wire somador_completo_1b_1_cout, somador_completo_1b_2_cout, somador_completo_1b_3_cout;

  somador_completo_1b somador_completo_1b_1 (
    .A(A[0]), .B(B[0]), .Cin(Cin), .S(S[0]), .Cout(somador_completo_1b_1_cout));
  somador_completo_1b somador_completo_1b_2 (
    .A(A[1]), .B(B[1]), .Cin(somador_completo_1b_1_cout), .S(S[1]), .Cout(somador_completo_1b_2_cout));
  somador_completo_1b somador_completo_1b_3 (
    .A(A[2]), .B(B[2]), .Cin(somador_completo_1b_2_cout), .S(S[2]), .Cout(somador_completo_1b_3_cout));
  somador_completo_1b somador_completo_1b_4 (
    .A(A[3]), .B(B[3]), .Cin(somador_completo_1b_3_cout), .S(S[3]), .Cout(Cout));
endmodule
