// Logisim project mips-pipeline.circ as structural Verilog: 12 circuits, main circuit mips
module alu (
  input  [3:0] ALU_Control,
  input  [31:0] in_2,
  input  [31:0] in_3,
  output [31:0] out_4,
  output Zero
);

  wire comparator_1_lt;
  wire [31:0] adder_1_out, and_1_out, multiplexer_1_out, or_1_out, subtractor_1_out, xor_1_out;

  assign and_1_out = in_2 & in_3;  // AND_Gate and_1, 32 bits wide
  assign or_1_out = in_2 | in_3;  // OR_Gate or_1, 32 bits wide
  Adder #(.width(32)) adder_1 (.a(in_2), .b(in_3), .out(adder_1_out));  // open: cin, cout
  Subtractor #(.width(32)) subtractor_1 (.a(in_2), .b(in_3), .out(subtractor_1_out));  // open: bin, bout
  Comparator #(.width(32), .mode("unsigned")) comparator_1 (.a(in_2), .b(in_3), .lt(comparator_1_lt));  // open: gt, eq
  assign xor_1_out = in_2 ^ in_3;  // XOR_Gate xor_1, 32 bits wide
  Multiplexer #(.width(32), .enable("false")) multiplexer_1 (
    .in0({32{1'b0}}), .in1(32'h1), .out(multiplexer_1_out), .sel(comparator_1_lt));
  Multiplexer #(.select(4), .width(32), .disabled(0), .enable("false")) multiplexer_2 (
    .in0(and_1_out), .in1(or_1_out), .in2(adder_1_out), .in6(subtractor_1_out), .in7(multiplexer_1_out),
    .in12(xor_1_out), .out(out_4), .sel(ALU_Control));  // open: in3, in4, in5, in8, in9, in10, in11, in13, in14, in15
  Comparator #(.width(32), .mode("unsigned")) comparator_2 (.a(out_4), .b({32{1'b0}}), .eq(Zero));  // open: gt, lt

  // Notes on the sheet:
  //   A
  //   B
  //   Logic from the first table in Chapter 4.4
  //   Op selects the result
  //   Output
endmodule

module mips (
);

  wire alu_1_zero, AlulSrc, and_1_out, clock_1_out, ex_mem_1_out_zero, RegDst, RegWrite, Restart_Program_out,
       Zero_Reg_File_out;
  wire [1:0] AlulOP, control_1_aluop, control_1_regwrite, ex_mem_1_out_wb, id_ex_1_out_wb;
  wire [1:1] mem_wb_1_out_wb;
  wire [2:0] control_1_branch, ex_mem_1_out_m, id_ex_1_out_m;
  wire [3:0] alu_control_1_operation, control_1_regdst;
  wire [4:0] ex_mem_1_out_dst, id_ex_1_out_instruction15_11, id_ex_1_out_instruction20_16, multiplexer_1_out,
       WriterReg;
  wire [31:0] adder_1_out, adder_2_out, adder_3_out, alu_1_out_4, bit_extender_1_out,
       ex_mem_1_out_alulresult, ex_mem_1_out_instruction, ex_mem_1_out_rd2, id_ex_1_out_instruction,
       id_ex_1_out_instruction15_0, id_ex_1_out_rd1, id_ex_1_out_rd2, mem_wb_1_out_adress, mem_wb_1_out_rd,
       multiplexer_2_out, multiplexer_3_out, multiplexer_4_out, PC_4, PC_q, ram_1_data, reg_32_1_readdata1,
       reg_32_1_readdata2, reg_if_id_1_out_instruction, rom_1_data, shifter_1_out, shifter_2_out;

  Register #(.width(32)) PC (
    .D(multiplexer_3_out), .Q(PC_q), .clk(clock_1_out), .clr(Restart_Program_out));  // open: en
  Clock clock_1 (.out(clock_1_out));
  Button Restart_Program (.out(Restart_Program_out));
  Button Zero_Reg_File (.out(Zero_Reg_File_out));
  Adder #(.width(32)) adder_1 (.a(PC_q), .b(32'h4), .out(adder_1_out));  // open: cin, cout
  ROM #(.dataWidth(32)) rom_1 (.addr(PC_q[9:2]), .data(rom_1_data));  // open: sel
  Reg_IF_ID reg_if_id_1 (
    .In_PC_4(adder_1_out), .In_Instruction(rom_1_data), .Out_PC_4(PC_4),
    .Out_Instruction(reg_if_id_1_out_instruction), .Clock(clock_1_out), .Clear(Zero_Reg_File_out));
  control control_1 (
    .in_1(reg_if_id_1_out_instruction[31:26]), .RegDst(control_1_regdst[0]), .Branch(control_1_branch[0]),
    .MemRead(control_1_branch[1]), .MemtoReg(control_1_regwrite[1]), .ALUOp(control_1_aluop),
    .MemWrite(control_1_branch[2]), .ALUSrc(control_1_regdst[3]), .RegWrite(control_1_regwrite[0]));
  // Probe on multiplexer_4_out
  // Probe on reg_if_id_1_out_instruction[15:0]
  reg_32 reg_32_1 (
    .ReadReg1(reg_if_id_1_out_instruction[25:21]), .ReadReg2(reg_if_id_1_out_instruction[20:16]),
    .WriteReg(WriterReg), .RegWrite(RegWrite), .ReadData1(reg_32_1_readdata1),
    .ReadData2(reg_32_1_readdata2), .WriteData(multiplexer_4_out), .Clk(clock_1_out),
    .Reset(Zero_Reg_File_out));
  // Probe on reg_if_id_1_out_instruction[25:21]
  // Probe on reg_if_id_1_out_instruction[20:16]
  // Probe on WriterReg
  assign bit_extender_1_out = {{16{reg_if_id_1_out_instruction[15]}}, reg_if_id_1_out_instruction[15:0]};  // Bit_Extender bit_extender_1
  ID_EX id_ex_1 (
    .In_WB(control_1_regwrite), .In_M(control_1_branch),
    .In_EX({control_1_regdst[3], control_1_aluop, control_1_regdst[0]}), .In_Instruction(PC_4),
    .ReadData1(reg_32_1_readdata1), .ReadData2(reg_32_1_readdata2), .ReadInstruction15_0(bit_extender_1_out),
    .ReadInstruction15_11(reg_if_id_1_out_instruction[15:11]), .Out_WB(id_ex_1_out_wb),
    .Out_M(id_ex_1_out_m), .Out_EX({AlulSrc, AlulOP, RegDst}), .Out_Instruction(id_ex_1_out_instruction),
    .Out_RD1(id_ex_1_out_rd1), .Out_RD2(id_ex_1_out_rd2), .Out_Instruction15_0(id_ex_1_out_instruction15_0),
    .Out_Instruction15_11(id_ex_1_out_instruction15_11), .Clock(clock_1_out), .Clear(Zero_Reg_File_out),
    .Out_Instruction20_16(id_ex_1_out_instruction20_16),
    .ReadInstruction20_16(reg_if_id_1_out_instruction[20:16]));
  // Probe on reg_32_1_readdata2
  // Probe on id_ex_1_out_rd2
  Multiplexer #(.width(5), .enable("false")) multiplexer_1 (
    .in0(id_ex_1_out_instruction20_16), .in1(id_ex_1_out_instruction15_11), .out(multiplexer_1_out),
    .sel(RegDst));
  // Probe on id_ex_1_out_instruction15_0
  Shifter #(.width(32)) shifter_1 (.in(id_ex_1_out_instruction15_0), .\dist (5'b00010), .out(shifter_1_out));
  Adder #(.width(32)) adder_2 (.a(id_ex_1_out_instruction), .b(shifter_2_out), .out(adder_2_out));  // open: cin, cout
  Shifter #(.width(32)) shifter_2 (.in(id_ex_1_out_instruction15_0), .\dist (5'b00010), .out(shifter_2_out));
  // Probe on id_ex_1_out_rd1
  alu alu_1 (
    .out_4(alu_1_out_4), .Zero(alu_1_zero), .in_2(id_ex_1_out_rd1), .in_3(multiplexer_2_out),
    .ALU_Control(alu_control_1_operation));
  Multiplexer #(.width(32), .enable("false")) multiplexer_2 (
    .in0(id_ex_1_out_rd2), .in1(id_ex_1_out_instruction15_0), .out(multiplexer_2_out), .sel(AlulSrc));
  // Probe on multiplexer_2_out
  alu_control alu_control_1 (
    .Operation(alu_control_1_operation), .ALUOp(AlulOP), .Function(id_ex_1_out_instruction15_0[5:0]));
  Adder #(.width(32)) adder_3 (.a(adder_1_out), .b(shifter_1_out), .out(adder_3_out));  // open: cin, cout
  // Probe on alu_control_1_operation
  EX_MEM ex_mem_1 (
    .In_WB(id_ex_1_out_wb), .In_M(id_ex_1_out_m), .In_Instruction(adder_2_out), .ALU_Zero(alu_1_zero),
    .ReadData2(id_ex_1_out_rd2), .Dst(multiplexer_1_out), .Out_WB(ex_mem_1_out_wb), .Out_M(ex_mem_1_out_m),
    .Out_Instruction(ex_mem_1_out_instruction), .Out_Zero(ex_mem_1_out_zero), .Out_RD2(ex_mem_1_out_rd2),
    .Out_Dst(ex_mem_1_out_dst), .Clock(clock_1_out), .Clear(Zero_Reg_File_out), .AlulResult(alu_1_out_4),
    .Out_AlulResult(ex_mem_1_out_alulresult));
  Multiplexer #(.width(32), .enable("false")) multiplexer_3 (
    .in0(adder_3_out), .in1(ex_mem_1_out_instruction), .out(multiplexer_3_out), .sel(and_1_out));
  and and_1 (and_1_out, ex_mem_1_out_m[0], ex_mem_1_out_zero);
  // Probe on multiplexer_3_out
  // Probe on ex_mem_1_out_alulresult[9:2]
  // Probe on ram_1_data
  RAM #(.dataWidth(32), .bus("separate")) ram_1 (
    .addr(ex_mem_1_out_alulresult[9:2]), .din(ex_mem_1_out_rd2), .data(ram_1_data), .str(ex_mem_1_out_m[2]),
    .clk(clock_1_out), .ld(ex_mem_1_out_m[1]));  // open: sel, clr
  MEM_WB mem_wb_1 (
    .In_WB(ex_mem_1_out_wb), .ReadData(ram_1_data), .Adress(ex_mem_1_out_alulresult), .Dst(ex_mem_1_out_dst),
    .Out_WB({mem_wb_1_out_wb[1], RegWrite}), .Out_RD(mem_wb_1_out_rd), .Out_Adress(mem_wb_1_out_adress),
    .Out_Dst(WriterReg), .Clock(clock_1_out), .Clear(Zero_Reg_File_out));
  Multiplexer #(.width(32), .enable("false")) multiplexer_4 (
    .in0(mem_wb_1_out_rd), .in1(mem_wb_1_out_adress), .out(multiplexer_4_out), .sel(mem_wb_1_out_wb[1]));
  // Probe on multiplexer_4_out

  // Notes on the sheet:
  //   Paulo Henrique Almeida de Andrade
  //   Clock
  //   Current Instruction
  //   contents of rom_1 (hex, n*v repeats v):
  //   8c090000 ac09000c
  //   Reg Write Data
  //   Imm. Value
  //   ALU Op
  //   MUX BEQ
  //   Next PC
  //   Mem Addr
endmodule

module instruction_type_decode (
  input  [5:0] opcode,
  output R_format,
  output lw,
  output sw,
  output beq
);

  Comparator #(.width(6), .mode("unsigned")) comparator_1 (.a({6{1'b0}}), .b(opcode), .eq(R_format));  // open: gt, lt
  Comparator #(.width(6), .mode("unsigned")) comparator_2 (.a(6'b100011), .b(opcode), .eq(lw));  // open: gt, lt
  Comparator #(.width(6), .mode("unsigned")) comparator_3 (.a(6'b101011), .b(opcode), .eq(sw));  // open: gt, lt
  Comparator #(.width(6), .mode("unsigned")) comparator_4 (.a(6'b000100), .b(opcode), .eq(beq));  // open: gt, lt

  // Notes on the sheet:
  //   This example sets "R-format" to true if opcode=00.
  //   ToDo: Fill in the logic from Fig 4.22 to determine the instruction type
  //   Hint: Use comparators and a constant to check for the right values
endmodule

module control_decode (
  input  Rformat,
  input  lw,
  input  sw,
  input  beq,
  output RegDst,
  output ALUSrc,
  output MemtoReg,
  output RegWrite,
  output MemRead,
  output MemWrite,
  output Branch,
  output ALUOp1,
  output ALUOp0
);

  wire not_2_out, not_3_out, not_5_out, not_6_out;

  not not_1 (RegDst, lw);
  not not_2 (not_2_out, Rformat);
  and and_1 (ALUSrc, not_2_out, not_3_out);
  not not_3 (not_3_out, beq);
  not not_4 (MemtoReg, Rformat);
  not not_5 (not_5_out, sw);
  and and_2 (RegWrite, not_5_out, not_6_out);
  not not_6 (not_6_out, beq);

  assign ALUOp0 = beq;
  assign ALUOp1 = Rformat;
  assign Branch = beq;
  assign MemRead = lw;
  assign MemWrite = sw;
endmodule

module alu_control (
  input  [5:0] Function,
  input  [1:0] ALUOp,
  output [3:0] Operation
);

  wire and_1_out, and_2_out, and_3_out, and_4_out, and_5_out, and_6_out, and_7_out, not_1_out, not_2_out,
       not_3_out, not_4_out, not_5_out, not_6_out, not_7_out, not_8_out, not_9_out, not_10_out, not_11_out,
       not_12_out, not_13_out, not_14_out, or_1_out, or_2_out;
  wire [2:0] priority_encoder_1_out;

  not not_1 (not_1_out, ALUOp[1]);
  not not_2 (not_2_out, ALUOp[0]);
  not not_3 (not_3_out, ALUOp[0]);
  not not_4 (not_4_out, Function[3]);
  not not_5 (not_5_out, Function[2]);
  not not_6 (not_6_out, Function[1]);
  not not_7 (not_7_out, Function[0]);
  not not_8 (not_8_out, ALUOp[1]);
  not not_9 (not_9_out, ALUOp[0]);
  not not_10 (not_10_out, Function[3]);
  not not_11 (not_11_out, ALUOp[0]);
  not not_12 (not_12_out, Function[0]);
  not not_13 (not_13_out, ALUOp[0]);
  not not_14 (not_14_out, ALUOp[0]);
  and and_1 (and_1_out, not_1_out, not_2_out);
  and and_2 (and_2_out, ALUOp[1], not_3_out, not_4_out, not_5_out, not_6_out, not_7_out);
  and and_3 (and_3_out, ALUOp[0], not_8_out);
  and and_4 (and_4_out, ALUOp[1], not_9_out, Function[5], not_10_out, Function[1]);
  and and_5 (and_5_out, ALUOp[1], not_11_out, Function[5], Function[2], not_12_out);
  and and_6 (and_6_out, ALUOp[1], not_13_out, Function[5], Function[2], Function[0]);
  and and_7 (and_7_out, ALUOp[1], not_14_out, Function[5], Function[3]);
  or or_1 (or_1_out, and_1_out, and_2_out);
  or or_2 (or_2_out, and_3_out, and_4_out);
  Priority_Encoder priority_encoder_1 (
    .in0(and_5_out), .in1(and_6_out), .in2(or_1_out), .in3(or_2_out), .in4(and_7_out),
    .out(priority_encoder_1_out));  // open: in5, in6, in7, en_in, gs, en_out
  Multiplexer #(.select(3), .width(4)) multiplexer_1 (
    .in0(4'b0000), .in1(4'b0001), .in2(4'b0010), .in3(4'b0110), .in4(4'b0111), .out(Operation),
    .sel(priority_encoder_1_out));  // open: in5, in6, in7, en

  // Notes on the sheet:
  //   Inputs
  //   B -- OR
  //   ToDo: Fill in logic from Fig 4.13
  //   Hint: Here is the logic for the first row: 
  //   A -- if (ALUOp1=0 and ALUOp0=0)
  //   D -- then output = 2 = 0010
  //   A
  //   C
  //   A
  //   C
  //   A
  //   A
  //   A
  //   C -- if (ALUOp1=1 and ALUOp0=0 and F3, F2, F1, F0 are all 0)
  //   B
  //   B
  //   True for 0010=2
  //   True for 0110=6
  //   True for 0001=1
  //   True for 0111=7
  //   True for 0000=0
  //   We have 5 possible outputs
  //   D
  //   Depending on which input is 1,
  //   one of the outputs above will be selected.
endmodule

module control (
  input  [5:0] in_1,
  output RegDst,
  output Branch,
  output MemRead,
  output MemtoReg,
  output [1:0] ALUOp,
  output MemWrite,
  output ALUSrc,
  output RegWrite
);

  wire instruction_type_decode_1_beq, instruction_type_decode_1_lw, instruction_type_decode_1_r_format,
       instruction_type_decode_1_sw;

  instruction_type_decode instruction_type_decode_1 (
    .opcode(in_1), .R_format(instruction_type_decode_1_r_format), .lw(instruction_type_decode_1_lw),
    .sw(instruction_type_decode_1_sw), .beq(instruction_type_decode_1_beq));
  control_decode control_decode_1 (
    .Rformat(instruction_type_decode_1_r_format), .RegDst(RegDst), .lw(instruction_type_decode_1_lw),
    .ALUSrc(ALUSrc), .sw(instruction_type_decode_1_sw), .MemtoReg(MemtoReg),
    .beq(instruction_type_decode_1_beq), .RegWrite(RegWrite), .MemRead(MemRead), .MemWrite(MemWrite),
    .Branch(Branch), .ALUOp1(ALUOp[1]), .ALUOp0(ALUOp[0]));

  // Notes on the sheet:
  //   Instruction OpCode
  //   Decode the Instruction Type first
  //   From the Insturction Type,
  //   decode the control signals
endmodule

module reg_32 (
  input  [4:0] ReadReg1,
  input  [4:0] ReadReg2,
  input  [4:0] WriteReg,
  input  RegWrite,
  input  [31:0] WriteData,
  input  Clk,
  input  Reset,
  output [31:0] ReadData1,
  output [31:0] ReadData2
);

  wire decoder_1_out0, decoder_1_out1, decoder_2_out0, decoder_2_out1, decoder_2_out2, decoder_2_out3,
       decoder_3_out0, decoder_3_out1, decoder_3_out2, decoder_3_out3, decoder_4_out0, decoder_4_out1,
       decoder_4_out2, decoder_4_out3, decoder_5_out0, decoder_5_out1, decoder_5_out2, decoder_5_out3,
       decoder_6_out0, decoder_6_out1, decoder_6_out2, decoder_6_out3, decoder_7_out0, decoder_7_out1,
       decoder_7_out2, decoder_7_out3, decoder_8_out0, decoder_8_out1, decoder_8_out2, decoder_8_out3,
       decoder_9_out0, decoder_9_out1, decoder_9_out2, decoder_9_out3, decoder_10_out0, decoder_10_out1,
       decoder_10_out2, decoder_10_out3, decoder_11_out0, decoder_11_out1, decoder_11_out2, decoder_11_out3;
  wire [31:0] multiplexer_1_out, multiplexer_2_out, multiplexer_3_out, multiplexer_4_out, multiplexer_5_out,
       multiplexer_6_out, multiplexer_7_out, multiplexer_8_out, multiplexer_9_out, multiplexer_10_out,
       multiplexer_13_out, multiplexer_14_out, multiplexer_15_out, multiplexer_16_out, multiplexer_17_out,
       multiplexer_18_out, multiplexer_19_out, multiplexer_20_out, multiplexer_21_out, multiplexer_22_out,
       register_1_q, register_2_q, register_3_q, register_4_q, register_5_q, register_6_q, register_7_q,
       register_8_q, register_9_q, register_10_q, register_11_q, register_12_q, register_13_q, register_14_q,
       register_15_q, register_16_q, register_17_q, register_18_q, register_19_q, register_20_q,
       register_21_q, register_22_q, register_23_q, register_24_q, register_25_q, register_26_q,
       register_27_q, register_28_q, register_29_q, register_30_q, register_31_q;

  // Probe on WriteReg
  Decoder #(.disabled(0)) decoder_1 (.out0(decoder_1_out0), .out1(decoder_1_out1), .sel(WriteReg[4]), .en(RegWrite));
  Decoder #(.select(2), .disabled(0)) decoder_2 (
    .out0(decoder_2_out0), .out1(decoder_2_out1), .out2(decoder_2_out2), .out3(decoder_2_out3),
    .sel(WriteReg[3:2]), .en(decoder_1_out0));
  Decoder #(.select(2), .disabled(0)) decoder_3 (
    .out0(decoder_3_out0), .out1(decoder_3_out1), .out2(decoder_3_out2), .out3(decoder_3_out3),
    .sel(WriteReg[1:0]), .en(decoder_2_out0));
  Decoder #(.select(2), .disabled(0)) decoder_4 (
    .out0(decoder_4_out0), .out1(decoder_4_out1), .out2(decoder_4_out2), .out3(decoder_4_out3),
    .sel(WriteReg[1:0]), .en(decoder_2_out1));
  Decoder #(.select(2), .disabled(0)) decoder_5 (
    .out0(decoder_5_out0), .out1(decoder_5_out1), .out2(decoder_5_out2), .out3(decoder_5_out3),
    .sel(WriteReg[1:0]), .en(decoder_2_out2));
  Decoder #(.select(2), .disabled(0)) decoder_6 (
    .out0(decoder_6_out0), .out1(decoder_6_out1), .out2(decoder_6_out2), .out3(decoder_6_out3),
    .sel(WriteReg[1:0]), .en(decoder_2_out3));
  Register #(.width(32)) register_1 (.D(WriteData), .en(decoder_3_out1), .Q(register_1_q), .clk(Clk), .clr(Reset));
  Register #(.width(32)) register_2 (.D(WriteData), .en(decoder_3_out2), .Q(register_2_q), .clk(Clk), .clr(Reset));
  Register #(.width(32)) register_3 (.D(WriteData), .en(decoder_3_out3), .Q(register_3_q), .clk(Clk), .clr(Reset));
  Register #(.width(32)) register_4 (.D(WriteData), .en(decoder_4_out0), .Q(register_4_q), .clk(Clk), .clr(Reset));
  Register #(.width(32)) register_5 (.D(WriteData), .en(decoder_4_out1), .Q(register_5_q), .clk(Clk), .clr(Reset));
  Register #(.width(32)) register_6 (.D(WriteData), .en(decoder_4_out2), .Q(register_6_q), .clk(Clk), .clr(Reset));
  Register #(.width(32)) register_7 (.D(WriteData), .en(decoder_4_out3), .Q(register_7_q), .clk(Clk), .clr(Reset));
  Register #(.width(32)) register_8 (.D(WriteData), .en(decoder_5_out0), .Q(register_8_q), .clk(Clk), .clr(Reset));
  Register #(.width(32)) register_9 (.D(WriteData), .en(decoder_5_out1), .Q(register_9_q), .clk(Clk), .clr(Reset));
  Register #(.width(32)) register_10 (.D(WriteData), .en(decoder_5_out2), .Q(register_10_q), .clk(Clk), .clr(Reset));
  Register #(.width(32)) register_11 (.D(WriteData), .en(decoder_5_out3), .Q(register_11_q), .clk(Clk), .clr(Reset));
  Register #(.width(32)) register_12 (.D(WriteData), .en(decoder_6_out0), .Q(register_12_q), .clk(Clk), .clr(Reset));
  Register #(.width(32)) register_13 (.D(WriteData), .en(decoder_6_out1), .Q(register_13_q), .clk(Clk), .clr(Reset));
  Register #(.width(32)) register_14 (.D(WriteData), .en(decoder_6_out2), .Q(register_14_q), .clk(Clk), .clr(Reset));
  Register #(.width(32)) register_15 (.D(WriteData), .en(decoder_6_out3), .Q(register_15_q), .clk(Clk), .clr(Reset));
  // Probe on {32{1'b0}}
  // Probe on register_1_q
  // Probe on register_2_q
  // Probe on register_3_q
  // Probe on register_4_q
  // Probe on register_5_q
  // Probe on register_6_q
  // Probe on register_7_q
  // Probe on register_8_q
  // Probe on register_9_q
  // Probe on register_10_q
  // Probe on register_11_q
  // Probe on register_12_q
  // Probe on register_13_q
  // Probe on register_14_q
  // Probe on register_15_q
  // Probe on ReadReg1
  Multiplexer #(.select(2), .width(32), .enable("false")) multiplexer_1 (
    .in0({32{1'b0}}), .in1(register_1_q), .in2(register_2_q), .in3(register_3_q), .out(multiplexer_1_out),
    .sel(ReadReg1[1:0]));
  Multiplexer #(.select(2), .width(32), .enable("false")) multiplexer_2 (
    .in0(register_4_q), .in1(register_5_q), .in2(register_6_q), .in3(register_7_q), .out(multiplexer_2_out),
    .sel(ReadReg1[1:0]));
  Multiplexer #(.select(2), .width(32), .enable("false")) multiplexer_3 (
    .in0(register_8_q), .in1(register_9_q), .in2(register_10_q), .in3(register_11_q),
    .out(multiplexer_3_out), .sel(ReadReg1[1:0]));
  Multiplexer #(.select(2), .width(32), .enable("false")) multiplexer_4 (
    .in0(register_12_q), .in1(register_13_q), .in2(register_14_q), .in3(register_15_q),
    .out(multiplexer_4_out), .sel(ReadReg1[1:0]));
  // Probe on ReadReg2
  Multiplexer #(.select(2), .width(32), .enable("false")) multiplexer_5 (
    .in0({32{1'b0}}), .in1(register_1_q), .in2(register_2_q), .in3(register_3_q), .out(multiplexer_5_out),
    .sel(ReadReg2[1:0]));
  Multiplexer #(.select(2), .width(32), .enable("false")) multiplexer_6 (
    .in0(register_4_q), .in1(register_5_q), .in2(register_6_q), .in3(register_7_q), .out(multiplexer_6_out),
    .sel(ReadReg2[1:0]));
  Multiplexer #(.select(2), .width(32), .enable("false")) multiplexer_7 (
    .in0(register_8_q), .in1(register_9_q), .in2(register_10_q), .in3(register_11_q),
    .out(multiplexer_7_out), .sel(ReadReg2[1:0]));
  Multiplexer #(.select(2), .width(32), .enable("false")) multiplexer_8 (
    .in0(register_12_q), .in1(register_13_q), .in2(register_14_q), .in3(register_15_q),
    .out(multiplexer_8_out), .sel(ReadReg2[1:0]));
  Multiplexer #(.select(2), .width(32), .enable("false")) multiplexer_9 (
    .in0(multiplexer_5_out), .in1(multiplexer_6_out), .in2(multiplexer_7_out), .in3(multiplexer_8_out),
    .out(multiplexer_9_out), .sel(ReadReg2[3:2]));
  Multiplexer #(.select(2), .width(32), .enable("false")) multiplexer_10 (
    .in0(multiplexer_1_out), .in1(multiplexer_2_out), .in2(multiplexer_3_out), .in3(multiplexer_4_out),
    .out(multiplexer_10_out), .sel(ReadReg1[3:2]));
  Decoder #(.select(2), .disabled(0)) decoder_7 (
    .out0(decoder_7_out0), .out1(decoder_7_out1), .out2(decoder_7_out2), .out3(decoder_7_out3),
    .sel(WriteReg[3:2]), .en(decoder_1_out1));
  Decoder #(.select(2), .disabled(0)) decoder_8 (
    .out0(decoder_8_out0), .out1(decoder_8_out1), .out2(decoder_8_out2), .out3(decoder_8_out3),
    .sel(WriteReg[1:0]), .en(decoder_7_out0));
  Decoder #(.select(2), .disabled(0)) decoder_9 (
    .out0(decoder_9_out0), .out1(decoder_9_out1), .out2(decoder_9_out2), .out3(decoder_9_out3),
    .sel(WriteReg[1:0]), .en(decoder_7_out1));
  Decoder #(.select(2), .disabled(0)) decoder_10 (
    .out0(decoder_10_out0), .out1(decoder_10_out1), .out2(decoder_10_out2), .out3(decoder_10_out3),
    .sel(WriteReg[1:0]), .en(decoder_7_out2));
  Decoder #(.select(2), .disabled(0)) decoder_11 (
    .out0(decoder_11_out0), .out1(decoder_11_out1), .out2(decoder_11_out2), .out3(decoder_11_out3),
    .sel(WriteReg[1:0]), .en(decoder_7_out3));
  Register #(.width(32)) register_16 (.D(WriteData), .en(decoder_8_out0), .Q(register_16_q), .clk(Clk), .clr(Reset));
  Register #(.width(32)) register_17 (.D(WriteData), .en(decoder_8_out1), .Q(register_17_q), .clk(Clk), .clr(Reset));
  Register #(.width(32)) register_18 (.D(WriteData), .en(decoder_8_out2), .Q(register_18_q), .clk(Clk), .clr(Reset));
  Register #(.width(32)) register_19 (.D(WriteData), .en(decoder_8_out3), .Q(register_19_q), .clk(Clk), .clr(Reset));
  Register #(.width(32)) register_20 (.D(WriteData), .en(decoder_9_out0), .Q(register_20_q), .clk(Clk), .clr(Reset));
  Register #(.width(32)) register_21 (.D(WriteData), .en(decoder_9_out1), .Q(register_21_q), .clk(Clk), .clr(Reset));
  Register #(.width(32)) register_22 (.D(WriteData), .en(decoder_9_out2), .Q(register_22_q), .clk(Clk), .clr(Reset));
  Register #(.width(32)) register_23 (.D(WriteData), .en(decoder_9_out3), .Q(register_23_q), .clk(Clk), .clr(Reset));
  Register #(.width(32)) register_24 (.D(WriteData), .en(decoder_10_out0), .Q(register_24_q), .clk(Clk), .clr(Reset));
  Register #(.width(32)) register_25 (.D(WriteData), .en(decoder_10_out1), .Q(register_25_q), .clk(Clk), .clr(Reset));
  Register #(.width(32)) register_26 (.D(WriteData), .en(decoder_10_out2), .Q(register_26_q), .clk(Clk), .clr(Reset));
  Register #(.width(32)) register_27 (.D(WriteData), .en(decoder_10_out3), .Q(register_27_q), .clk(Clk), .clr(Reset));
  Register #(.width(32)) register_28 (.D(WriteData), .en(decoder_11_out0), .Q(register_28_q), .clk(Clk), .clr(Reset));
  Register #(.width(32)) register_29 (.D(WriteData), .en(decoder_11_out1), .Q(register_29_q), .clk(Clk), .clr(Reset));
  Register #(.width(32)) register_30 (.D(WriteData), .en(decoder_11_out2), .Q(register_30_q), .clk(Clk), .clr(Reset));
  Register #(.width(32)) register_31 (.D(WriteData), .en(decoder_11_out3), .Q(register_31_q), .clk(Clk), .clr(Reset));
  // Probe on register_16_q
  // Probe on register_17_q
  // Probe on register_18_q
  // Probe on register_19_q
  // Probe on register_20_q
  // Probe on register_21_q
  // Probe on register_22_q
  // Probe on register_23_q
  // Probe on register_24_q
  // Probe on register_25_q
  // Probe on register_26_q
  // Probe on register_27_q
  // Probe on register_28_q
  // Probe on register_29_q
  // Probe on register_30_q
  // Probe on register_31_q
  Multiplexer #(.width(32), .enable("false")) multiplexer_11 (
    .in0(multiplexer_10_out), .in1(multiplexer_21_out), .out(ReadData1), .sel(ReadReg1[4]));
  Multiplexer #(.width(32), .enable("false")) multiplexer_12 (
    .in0(multiplexer_9_out), .in1(multiplexer_22_out), .out(ReadData2), .sel(ReadReg2[4]));
  Multiplexer #(.select(2), .width(32), .enable("false")) multiplexer_13 (
    .in0(register_16_q), .in1(register_17_q), .in2(register_18_q), .in3(register_19_q),
    .out(multiplexer_13_out), .sel(ReadReg1[1:0]));
  Multiplexer #(.select(2), .width(32), .enable("false")) multiplexer_14 (
    .in0(register_20_q), .in1(register_21_q), .in2(register_22_q), .in3(register_23_q),
    .out(multiplexer_14_out), .sel(ReadReg1[1:0]));
  Multiplexer #(.select(2), .width(32), .enable("false")) multiplexer_15 (
    .in0(register_24_q), .in1(register_25_q), .in2(register_26_q), .in3(register_27_q),
    .out(multiplexer_15_out), .sel(ReadReg1[1:0]));
  Multiplexer #(.select(2), .width(32), .enable("false")) multiplexer_16 (
    .in0(register_28_q), .in1(register_29_q), .in2(register_30_q), .in3(register_31_q),
    .out(multiplexer_16_out), .sel(ReadReg1[1:0]));
  Multiplexer #(.select(2), .width(32), .enable("false")) multiplexer_17 (
    .in0(register_16_q), .in1(register_17_q), .in2(register_18_q), .in3(register_19_q),
    .out(multiplexer_17_out), .sel(ReadReg2[1:0]));
  Multiplexer #(.select(2), .width(32), .enable("false")) multiplexer_18 (
    .in0(register_20_q), .in1(register_21_q), .in2(register_22_q), .in3(register_23_q),
    .out(multiplexer_18_out), .sel(ReadReg2[1:0]));
  Multiplexer #(.select(2), .width(32), .enable("false")) multiplexer_19 (
    .in0(register_24_q), .in1(register_25_q), .in2(register_26_q), .in3(register_27_q),
    .out(multiplexer_19_out), .sel(ReadReg2[1:0]));
  Multiplexer #(.select(2), .width(32), .enable("false")) multiplexer_20 (
    .in0(register_28_q), .in1(register_29_q), .in2(register_30_q), .in3(register_31_q),
    .out(multiplexer_20_out), .sel(ReadReg2[1:0]));
  Multiplexer #(.select(2), .width(32), .enable("false")) multiplexer_21 (
    .in0(multiplexer_17_out), .in1(multiplexer_18_out), .in2(multiplexer_19_out), .in3(multiplexer_20_out),
    .out(multiplexer_21_out), .sel(ReadReg2[3:2]));
  Multiplexer #(.select(2), .width(32), .enable("false")) multiplexer_22 (
    .in0(multiplexer_13_out), .in1(multiplexer_14_out), .in2(multiplexer_15_out), .in3(multiplexer_16_out),
    .out(multiplexer_22_out), .sel(ReadReg1[3:2]));

  // Notes on the sheet:
  //   $2 = $v0
  //   $3 = $v1
  //   $0 = $zero
  //   $8 = $t0
  //   $16 = $s0
endmodule

module Testes (
  input  in_1,
  input  [4:0] in_2,
  input  [4:0] in_3,
  input  [4:0] in_4,
  input  [31:0] in_5,
  input  [31:0] A,
  input  [31:0] B,
  input  [3:0] Alu_OP
);

  wire alu_1_zero, button_1_out, clock_1_out;
  wire [31:0] alu_1_out_4, reg_32_1_readdata1, reg_32_1_readdata2;

  Clock clock_1 (.out(clock_1_out));
  Button button_1 (.out(button_1_out));
  // Probe on in_2
  // Probe on in_3
  // Probe on in_4
  // Probe on in_5
  reg_32 reg_32_1 (
    .ReadReg1(in_2), .ReadReg2(in_3), .WriteReg(in_4), .RegWrite(in_1), .ReadData1(reg_32_1_readdata1),
    .ReadData2(reg_32_1_readdata2), .WriteData(in_5), .Clk(clock_1_out), .Reset(button_1_out));
  // Probe on A
  // Probe on B
  alu alu_1 (.out_4(alu_1_out_4), .Zero(alu_1_zero), .in_2(A), .in_3(B), .ALU_Control(Alu_OP));
  // Probe on reg_32_1_readdata1
  // Probe on reg_32_1_readdata2
  // Probe on alu_1_zero
  // Probe on alu_1_out_4
endmodule

module Reg_IF_ID (
  input  [31:0] In_PC_4,
  input  [31:0] In_Instruction,
  input  Clock,
  input  Clear,
  output [31:0] Out_PC_4,
  output [31:0] Out_Instruction
);

  Register #(.width(32)) register_1 (.D(In_PC_4), .Q(Out_PC_4), .clk(Clock), .clr(Clear));  // open: en
  Register #(.width(32)) register_2 (.D(In_Instruction), .Q(Out_Instruction), .clk(Clock), .clr(Clear));  // open: en
endmodule

module ID_EX (
  input  [1:0] In_WB,
  input  [2:0] In_M,
  input  [3:0] In_EX,
  input  [31:0] In_Instruction,
  input  [31:0] ReadData1,
  input  [31:0] ReadData2,
  input  [31:0] ReadInstruction15_0,
  input  [4:0] ReadInstruction20_16,
  input  [4:0] ReadInstruction15_11,
  input  Clock,
  input  Clear,
  output [1:0] Out_WB,
  output [2:0] Out_M,
  output [3:0] Out_EX,
  output [31:0] Out_Instruction,
  output [31:0] Out_RD1,
  output [31:0] Out_RD2,
  output [31:0] Out_Instruction15_0,
  output [4:0] Out_Instruction20_16,
  output [4:0] Out_Instruction15_11
);

  Register #(.width(2)) register_1 (.D(In_WB), .Q(Out_WB), .clk(Clock), .clr(Clear));  // open: en
  Register #(.width(3)) register_2 (.D(In_M), .Q(Out_M), .clk(Clock), .clr(Clear));  // open: en
  Register #(.width(4)) register_3 (.D(In_EX), .Q(Out_EX), .clk(Clock), .clr(Clear));  // open: en
  Register #(.width(32)) register_4 (.D(In_Instruction), .Q(Out_Instruction), .clk(Clock), .clr(Clear));  // open: en
  Register #(.width(32)) register_5 (.D(ReadData1), .Q(Out_RD1), .clk(Clock), .clr(Clear));  // open: en
  Register #(.width(32)) register_6 (.D(ReadData2), .Q(Out_RD2), .clk(Clock), .clr(Clear));  // open: en
  Register #(.width(32)) register_7 (
    .D(ReadInstruction15_0), .Q(Out_Instruction15_0), .clk(Clock), .clr(Clear));  // open: en
  Register #(.width(5)) register_8 (
    .D(ReadInstruction20_16), .Q(Out_Instruction20_16), .clk(Clock), .clr(Clear));  // open: en
  Register #(.width(5)) register_9 (
    .D(ReadInstruction15_11), .Q(Out_Instruction15_11), .clk(Clock), .clr(Clear));  // open: en
endmodule

module EX_MEM (
  input  [1:0] In_WB,
  input  [2:0] In_M,
  input  [31:0] In_Instruction,
  input  ALU_Zero,
  input  [31:0] AlulResult,
  input  [31:0] ReadData2,
  input  [4:0] Dst,
  input  Clock,
  input  Clear,
  output [1:0] Out_WB,
  output [2:0] Out_M,
  output [31:0] Out_Instruction,
  output Out_Zero,
  output [31:0] Out_AlulResult,
  output [31:0] Out_RD2,
  output [4:0] Out_Dst
);

  wire [31:0] undriven;

  Register #(.width(2)) register_1 (.D(In_WB), .Q(Out_WB), .clk(Clock), .clr(Clear));  // open: en
  Register #(.width(3)) register_2 (.D(In_M), .Q(Out_M), .clk(Clock), .clr(Clear));  // open: en
  Register #(.width(32)) register_3 (.D(undriven), .Q(Out_Instruction), .clk(Clock), .clr(Clear));  // open: en
  Register #(.width(1)) register_4 (.D(ALU_Zero), .Q(Out_Zero), .clk(Clock), .clr(Clear));  // open: en
  Register #(.width(32)) register_5 (.D(AlulResult), .Q(Out_AlulResult), .clk(Clock), .clr(Clear));  // open: en
  Register #(.width(32)) register_6 (.D(ReadData2), .Q(Out_RD2), .clk(Clock), .clr(Clear));  // open: en
  Register #(.width(5)) register_7 (.D(Dst), .Q(Out_Dst), .clk(Clock), .clr(Clear));  // open: en
endmodule

module MEM_WB (
  input  [1:0] In_WB,
  input  [31:0] ReadData,
  input  [31:0] Adress,
  input  [4:0] Dst,
  input  Clock,
  input  Clear,
  output [1:0] Out_WB,
  output [31:0] Out_RD,
  output [31:0] Out_Adress,
  output [4:0] Out_Dst
);

  Register #(.width(2)) register_1 (.D(In_WB), .Q(Out_WB), .clk(Clock), .clr(Clear));  // open: en
  Register #(.width(32)) register_2 (.D(ReadData), .Q(Out_RD), .clk(Clock), .clr(Clear));  // open: en
  Register #(.width(32)) register_3 (.D(Adress), .Q(Out_Adress), .clk(Clock), .clr(Clear));  // open: en
  Register #(.width(5)) register_4 (.D(Dst), .Q(Out_Dst), .clk(Clock), .clr(Clear));  // open: en
endmodule
